// Logisim project ComputerProject_TEST_syncclk_n_button.circ as structural Verilog
module CPU (
);

  wire dipswitch_1_sw1, dipswitch_1_sw2, undriven;
  wire [7:0] math_logic_sys_1_alu_out, math_logic_sys_1_alu_ra, math_logic_sys_1_alu_rb,
       math_logic_sys_1_ra_val, math_logic_sys_1_rb_val, math_logic_sys_1_rc_val, math_logic_sys_1_rd_val,
       output_register_curr_val;

  DipSwitch #(.number(2)) dipswitch_1 (.sw1(dipswitch_1_sw1), .sw2(dipswitch_1_sw2));
  // Probe on undriven
  // Probe on undriven
  clk Clock (.HLT(dipswitch_1_sw1));  // open: Clock_pos, Clock_neg
  Register_Template output_register (.curr_val(output_register_curr_val));  // open: WE, CLK, RST, OE, data_bus_in, data_bus_out
  Math_Logic_Sys math_logic_sys_1 (
    .data_in(math_logic_sys_1_alu_out), .RA_Val(math_logic_sys_1_ra_val), .RB_Val(math_logic_sys_1_rb_val),
    .ALU_RA(math_logic_sys_1_alu_ra), .ALU_RB(math_logic_sys_1_alu_rb), .ALU_OUT(math_logic_sys_1_alu_out),
    .data_bus_out(math_logic_sys_1_alu_out), .RC_val(math_logic_sys_1_rc_val),
    .RD_val(math_logic_sys_1_rd_val));  // open: REG_OP, clk, ALU_OP, reset
  // Probe on output_register_curr_val
  // Probe on output_register_curr_val
  // Probe on math_logic_sys_1_ra_val
  // Probe on math_logic_sys_1_ra_val
  // Probe on math_logic_sys_1_alu_ra
  // Probe on math_logic_sys_1_alu_ra
  // Probe on math_logic_sys_1_rc_val
  // Probe on math_logic_sys_1_rc_val
  // Probe on math_logic_sys_1_rd_val
  // Probe on math_logic_sys_1_rd_val
  // Probe on math_logic_sys_1_rb_val
  // Probe on math_logic_sys_1_rb_val
  // Probe on math_logic_sys_1_alu_rb
  // Probe on math_logic_sys_1_alu_rb

  // Notes on the sheet:
  //   GPIO Registers
  //   A
  //   B
  //   C
  //   D
  //   ALU Internal Registers
  //   A
  //   B
endmodule

module clk (
  input  HLT,
  output Clock_pos,
  output Clock_neg
);

  wire and_1_out, and_2_out, and_3_out, button_1_out, clock_1_out, controlled_buffer_2_out, dipswitch_1_sw1,
       dipswitch_1_sw2, nand_1_out, nand_2_out, nand_3_out, nand_4_out, not_1_out, not_2_out, not_3_out,
       not_4_out, pull_resistor_1_node, pull_resistor_2_node, pull_resistor_3_node, t_ff_1_q, t_ff_1_qn,
       xor_1_out, xor_2_out, xor_3_out, xor_4_out, xor_5_out;

  xor xor_1 (xor_1_out, t_ff_1_qn, t_ff_1_q);
  T_Flip_Flop t_ff_1 (.T(xor_1_out), .clk(pull_resistor_1_node), .Q(t_ff_1_q), .Qn(t_ff_1_qn));  // open: reset, preset
  Pull_Resistor pull_resistor_1 (.node(pull_resistor_1_node));
  not not_1 (not_1_out, HLT);
  assign pull_resistor_1_node = pull_resistor_3_node ? button_1_out : 1'bz;  // Controlled_Buffer controlled_buffer_1
  Button button_1 (.out(button_1_out));
  Clock #(.highDuration(2), .lowDuration(2)) clock_1 (.out(clock_1_out));
  assign controlled_buffer_2_out = pull_resistor_2_node ? clock_1_out : 1'bz;  // Controlled_Buffer controlled_buffer_2
  Pull_Resistor pull_resistor_2 (.node(pull_resistor_2_node));
  Pull_Resistor pull_resistor_3 (.node(pull_resistor_3_node));
  assign pull_resistor_2_node = HLT ? dipswitch_1_sw1 : 1'bz;  // Controlled_Buffer controlled_buffer_3
  assign pull_resistor_3_node = HLT ? dipswitch_1_sw2 : 1'bz;  // Controlled_Buffer controlled_buffer_4
  DipSwitch #(.number(2)) dipswitch_1 (.sw1(dipswitch_1_sw1), .sw2(dipswitch_1_sw2));
  Pull_Resistor pull_resistor_4 (.node(controlled_buffer_2_out));
  xor xor_2 (xor_2_out, pull_resistor_2_node, pull_resistor_3_node);
  and and_1 (and_1_out, pull_resistor_3_node, pull_resistor_2_node);
  xor xor_3 (xor_3_out, controlled_buffer_2_out, t_ff_1_q);
  LED Run (.in(pull_resistor_2_node));
  not not_2 (not_2_out, pull_resistor_2_node);
  xor xor_4 (xor_4_out, not_1_out, and_1_out);
  not not_3 (not_3_out, clock_1_out);
  not not_4 (not_4_out, xor_3_out);
  LED Stop (.in(xor_5_out));
  xor xor_5 (xor_5_out, not_2_out, not_1_out);
  and and_2 (and_2_out, xor_4_out, nand_3_out);
  and and_3 (and_3_out, nand_4_out, xor_4_out);
  LED Halt (.in(not_1_out));
  xor xor_6 (Clock_pos, and_2_out, nand_3_out);
  xor xor_7 (Clock_neg, nand_4_out, and_3_out);
  nand nand_1 (nand_1_out, xor_3_out, clock_1_out, xor_2_out);
  nand nand_2 (nand_2_out, xor_2_out, not_3_out, not_4_out);
  LED clk_pos (.in(Clock_pos));
  nand nand_3 (nand_3_out, nand_4_out, nand_1_out);
  nand nand_4 (nand_4_out, nand_3_out, nand_2_out);
  LED clk_neg (.in(Clock_neg));

  // Notes on the sheet:
  //   HLT: pull=up
  //   Oscillation during half stop
  //   Halt line tick
endmodule

module Register_Template (
  input  [7:0] data_bus_in,
  input  [7:0] data_bus_out,
  input  WE,
  input  CLK,
  input  RST,
  input  OE,
  output [7:0] curr_val
);

  Register register_1 (.D(data_bus_in), .en(WE), .clk(CLK), .Q(curr_val), .clr(RST));
  assign data_bus_out = OE ? curr_val : 8'bz;  // Controlled_Buffer controlled_buffer_1
endmodule

module ALU (
  input  [7:0] A,
  input  [7:0] B,
  input  clk,
  input  ALU_OP_2,
  input  bus_write,
  input  reset,
  input  bus_read,
  input  AB_select,
  output [7:0] ALU_RA,
  output [7:0] ALU_RB,
  output [7:0] y
);

  wire and_1_out, and_2_out, demultiplexer_1_out0, demultiplexer_1_out1;
  wire [7:0] adder_1_out, multiplexer_1_out, multiplier_1_out;

  Demultiplexer #(.enable("false")) demultiplexer_1 (
    .out0(demultiplexer_1_out0), .out1(demultiplexer_1_out1), .in(1'b1), .sel(AB_select));
  and and_1 (and_1_out, bus_read, demultiplexer_1_out0);
  and and_2 (and_2_out, demultiplexer_1_out1, bus_read);
  Register register_1 (.D(A), .en(and_1_out), .clk(clk), .Q(ALU_RA), .clr(reset));
  Register register_2 (.D(B), .en(and_2_out), .clk(clk), .Q(ALU_RB), .clr(reset));
  Adder adder_1 (.a(ALU_RA), .b(ALU_RB), .out(adder_1_out));  // open: cin, cout
  Multiplier multiplier_1 (.a(ALU_RA), .b(ALU_RB), .out(multiplier_1_out));  // open: cin, cout
  Multiplexer #(.enable("false"), .width(8)) multiplexer_1 (
    .in0(adder_1_out), .in1(multiplier_1_out), .out(multiplexer_1_out), .sel(ALU_OP_2));
  assign y = bus_write ? multiplexer_1_out : 8'bz;  // Controlled_Buffer controlled_buffer_1

  // Notes on the sheet:
  //   bus_read: pull=down
  //   A: pull=down
  //   B: pull=down
  //   clk: pull=down
  //   ALU_OP_2: pull=down
  //   bus_write: pull=down
  //   reset: pull=down
  //   0 = add
  //   1 = mul
endmodule

module TwosCompConverter (
  input  [7:0] data_in,
  output [7:0] data_out
);

  wire [7:0] not_1_out;

  Pull_Resistor pull_resistor_1 (.node(data_in));
  assign not_1_out = ~data_in;  // NOT_Gate not_1, 8 bits wide
  Adder adder_1 (.a(not_1_out), .b(8'h1), .out(data_out));  // open: cin, cout

  // Notes on the sheet:
  //   data_in: pull=down
endmodule

module Math_Logic_Sys (
  input  [7:0] data_in,
  input  [3:0] REG_OP,
  input  clk,
  input  [11:0] ALU_OP,
  input  reset,
  output [7:0] RA_Val,
  output [7:0] RB_Val,
  output [7:0] ALU_RA,
  output [7:0] ALU_RB,
  output [7:0] ALU_OUT,
  output [7:0] data_bus_out,
  output [7:0] RC_val,
  output [7:0] RD_val
);

  wire demultiplexer_1_out0, demultiplexer_1_out1, demultiplexer_2_out0, demultiplexer_2_out1,
       demultiplexer_2_out2, demultiplexer_2_out3, demultiplexer_3_out0, demultiplexer_3_out1,
       demultiplexer_3_out2, demultiplexer_3_out3;

  Demultiplexer demultiplexer_1 (
    .out0(demultiplexer_1_out0), .out1(demultiplexer_1_out1), .in(1'b1), .sel(REG_OP[0]), .en(REG_OP[3]));
  Demultiplexer #(.select(2)) demultiplexer_2 (
    .out0(demultiplexer_2_out0), .out1(demultiplexer_2_out1), .out2(demultiplexer_2_out2),
    .out3(demultiplexer_2_out3), .in(1'b1), .sel(REG_OP[2:1]), .en(demultiplexer_1_out0));
  Demultiplexer #(.select(2)) demultiplexer_3 (
    .out0(demultiplexer_3_out0), .out1(demultiplexer_3_out1), .out2(demultiplexer_3_out2),
    .out3(demultiplexer_3_out3), .in(1'b1), .sel(REG_OP[2:1]), .en(demultiplexer_1_out1));
  Register_Template RA (
    .curr_val(RA_Val), .WE(demultiplexer_2_out0), .CLK(clk), .RST(reset), .OE(demultiplexer_3_out0),
    .data_bus_in(data_in), .data_bus_out(data_bus_out));
  Register_Template RB (
    .curr_val(RB_Val), .WE(demultiplexer_2_out1), .CLK(clk), .RST(reset), .OE(demultiplexer_3_out1),
    .data_bus_in(data_in), .data_bus_out(data_bus_out));
  Register_Template RC (
    .curr_val(RC_val), .WE(demultiplexer_2_out2), .CLK(clk), .RST(reset), .OE(demultiplexer_3_out2),
    .data_bus_in(data_in), .data_bus_out(data_bus_out));
  Register_Template RD (
    .curr_val(RD_val), .WE(demultiplexer_2_out3), .CLK(clk), .RST(reset), .OE(demultiplexer_3_out3),
    .data_bus_in(data_in), .data_bus_out(data_bus_out));
  ALU alu_1 (
    .ALU_RA(ALU_RA), .ALU_RB(ALU_RB), .y(ALU_OUT));  // open: A, B, clk, ALU_OP_2, bus_write, reset, bus_read, AB_select

  // Notes on the sheet:
  //   REG_OP: pull=down
  //   ALU_OP: pull=down
endmodule
